# Fritzing sketch raspberry (saved by Fritzing 0.9.6b)
breadboards: 1

parts:
  Mod1 = Raspberry Pi Pico
  U1 = POT_SWITCH [package=pot_pth]
  LED1 = smd LED [color="Red (633nm)" package="1206 [SMD]"]
  LED2 = smd LED [color="Green (560nm)" package="1206 [SMD]"]
  LED3 = smd LED [color="Blue (470nm)" package="1206 [SMD]"]

nets:
  N1: Mod1.pin_1, LED1.anode
  N2: Mod1.pin_2, LED2.anode
  N3: Mod1.pin_3, Mod1.pin_8, Mod1.pin_13, Mod1.pin_18, Mod1.pin_23, Mod1.pin_28, Mod1.pin_33, Mod1.pin_38, Mod1.pin_42, U1.G$1_E, LED1.cathode, LED2.cathode, LED3.cathode
  N4: Mod1.pin_4, LED3.anode
  N5: Mod1.pin_31, U1.G$2_1
  N6: Mod1.pin_36, U1.G$1_A, U1.G$2_2, U1.G$1_S

custom parts:
  Raspberry Pi Pico: Raspberry Pi Pico. Based around the RP2040 microcontroller the Pico is a low cost microcontroller device bringing Raspberry Pi quality, cost, and easy of use to the microcontroller space. Jan 2021, Split part in to two versions: tht (this one) and SMD. This one will drill holes for a .1 in header in pcb to allow plugging in the module as well as providing pads to solder the module to the top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
